# Fritzing sketch fan layout (saved by Fritzing 0.9.2b)
circuit board: 2.61cm x 3.86cm
breadboards: 1

parts:
  J1 = female pin header, 8 pins [form="♀ (female)"]  # not connected
  J2 = female pin header, 8 pins [form="♀ (female)"]  # not connected
  J5 = female pin header, 5 pins [form="♀ (female)"]  # not connected
  R13 = Resistor [tolerance=±5% resistance=220 package=THT]
  Q11 = NPN-Transistor [package="TO92 [THT]"]
  R14 = Resistor [tolerance=±5% resistance=220 package=THT]
  Q12 = NPN-Transistor [package="TO92 [THT]"]
  R15 = Resistor [tolerance=±5% resistance=220 package=THT]
  Q13 = NPN-Transistor [package="TO92 [THT]"]
  R16 = Resistor [tolerance=±5% resistance=220 package=THT]
  Q14 = NPN-Transistor [package="TO92 [THT]"]
  R17 = Resistor [tolerance=±5% resistance=220 package=THT]
  Q15 = NPN-Transistor [package="TO92 [THT]"]
  R18 = Resistor [tolerance=±5% resistance=220 package=THT]
  Q16 = NPN-Transistor [package="TO92 [THT]"]
  R19 = Resistor [tolerance=±5% resistance=220 package=THT]
  Q17 = NPN-Transistor [package="TO92 [THT]"]
  J9 = female pin header, 10 pins [form="♀ (female)"]  # not connected
  c1 = Ceramic Capacitor [capacitance=100nF package="100 mil [THT, multilayer]"]  # not connected
  C1 = Electrolytic Capacitor [capacitance=1µF package="100 mil [THT, electrolytic]"]  # not connected

nets:
  N1: R13.Pin_0, Q11.B
  N2: R14.Pin_0, Q12.B
  N3: Q12.E, Q13.E
  N4: R15.Pin_0, Q13.B
  N5: R16.Pin_0, Q14.B
  N6: Q14.E, Q15.E, Q16.E, Q17.E
  N7: R17.Pin_0, Q15.B
  N8: R18.Pin_0, Q16.B
  N9: R19.Pin_0, Q17.B
