# Fritzing sketch fan (saved by Fritzing 0.9.6b)
circuit board: 11.4441cm x 6.95677cm
breadboards: 1

parts:
  C3 = Ceramic Capacitor [capacitance=0.1µF package="1206 [SMD, multilayer]"]
  C4 = Capacitor Polarized [part_number=1000μF package=panasonic_h13]
  U17 = ESP8266 WiFi Module [part_number=ESP8266]
  Q1 = PNP-Transistor [package="TO92 [THT]"]
  HI = Resistor [tolerance=±5% resistance=10k power=0.25 package=THT]
  Q2 = PNP-Transistor [package="TO92 [THT]"]
  MED = Resistor [tolerance=±5% resistance=10k power=0.25 package=THT]
  5 = Header 1 [package=1x01_offset]
  Q3 = PNP-Transistor [package="TO92 [THT]"]
  LOW = Resistor [tolerance=±5% resistance=10k power=0.25 package=THT]
  3 = Header 1 [package=1x01_offset]
  4 = Header 1 [package=1x01_offset]
  Q4 = PNP-Transistor [package="TO92 [THT]"]
  OFF = Resistor [tolerance=±5% resistance=10k power=0.25 package=THT]
  3_2 = Header 1 [package=1x01_offset]
  2 = Header 1 [package=1x01_offset]
  Q5 = PNP-Transistor [package="TO92 [THT]"]
  REV = Resistor [tolerance=±5% resistance=10k power=0.25 package=THT]
  1 = Header 1 [package=1x01_offset]
  8 = Header 1 [package=1x01_offset]
  Q6 = PNP-Transistor [package="TO92 [THT]"]
  UP = Resistor [tolerance=±5% resistance=10k power=0.25 package=THT]
  7 = Header 1 [package=1x01_offset]
  8_2 = Header 1 [package=1x01_offset]
  Q7 = PNP-Transistor [package="TO92 [THT]"]
  DOWN = Resistor [tolerance=±5% resistance=10k power=0.25 package=THT]
  2_2 = Header 1 [package=1x01_offset]
  4_2 = Header 1 [package=1x01_offset]
  1_2 = Header 1 [package=1x01_offset]
  1_3 = Header 1 [package=1x01_offset]
  1_4 = Header 1 [package=1x01_offset]
  GND = Header 1 [package=1x01_offset]
  VCC = Header 1 [package=1x01_offset]
  R1 = Resistor [tolerance=±5% resistance=10k power=0.25 package=THT]
  DS2 = DS18B20 1-Wire Temperature Sensor [part_number=DS18B20]
  R9 = Resistor [tolerance=±5% resistance=4.7k power=0.25 package=THT]

nets:
  GND: C3.0, C4.-, U17.GND, GND.1, DS2.GND
  3.3V: C3.1, C4.+, U17.VCC, U17.CH_PD, U17.REST, VCC.1, R1.Pin_0, DS2.VDD, R9.Pin_0
  N1: U17.GPIO_0, R1.Pin_1
  N2: U17.GPIO_2, DS2.DQ, R9.Pin_1
  N3: U17.GPIO_15, LOW.Pin_0
  N4: U17.GPIO_4, HI.Pin_0
  N5: U17.GPIO_5, MED.Pin_0
  N6: U17.GPIO_16, DOWN.Pin_0
  N7: U17.GPIO_14, UP.Pin_0
  N8: U17.GPIO_12, REV.Pin_0
  N9: U17.GPIO_13, OFF.Pin_0
  N10: Q1.E, 1_4.1
  N11: Q1.B, HI.Pin_1
  N12: Q1.C, 4_2.1
  N13: Q2.E, 1_3.1
  N14: Q2.B, MED.Pin_1
  N15: Q2.C, 2_2.1
  N16: 5.1, Q3.C
  N17: Q3.E, 1_2.1
  N18: Q3.B, LOW.Pin_1
  N19: 3.1, Q4.E
  N20: 4.1, Q4.C
  N21: Q4.B, OFF.Pin_1
  N22: 3_2.1, Q5.E
  N23: 2.1, Q5.C
  N24: Q5.B, REV.Pin_1
  N25: 1.1, Q6.E
  N26: 8.1, Q6.C
  N27: Q6.B, UP.Pin_1
  N28: 7.1, Q7.E
  N29: 8_2.1, Q7.C
  N30: Q7.B, DOWN.Pin_1

custom parts:
  ESP8266 WiFi Module: Generic WiFi Module based on the ESP8266 with onboard PCB antenna and UART communications
